# Fritzing sketch led-matrix (saved by Fritzing 0.8.7b)
breadboards: 1

parts:
  LED1 = LED - 5mm [color="Red (633nm)" package="5 mm [THT]"]
  LED2 = LED - 5mm [color="Red (633nm)" package="5 mm [THT]"]
  LED3 = LED - 5mm [color="Red (633nm)" package="5 mm [THT]"]
  LED4 = LED - 5mm [color="Red (633nm)" package="5 mm [THT]"]
  LED5 = LED - 5mm [color="Red (633nm)" package="5 mm [THT]"]
  LED6 = LED - 5mm [color="Red (633nm)" package="5 mm [THT]"]
  LED7 = LED - 5mm [color="Red (633nm)" package="5 mm [THT]"]
  LED8 = LED - 5mm [color="Red (633nm)" package="5 mm [THT]"]
  LED9 = LED - 5mm [color="Red (633nm)" package="5 mm [THT]"]
  LED10 = LED - 5mm [color="Red (633nm)" package="5 mm [THT]"]
  LED11 = LED - 5mm [color="Red (633nm)" package="5 mm [THT]"]
  LED12 = LED - 5mm [color="Red (633nm)" package="5 mm [THT]"]
  LED13 = LED - 5mm [color="Red (633nm)" package="5 mm [THT]"]
  LED14 = LED - 5mm [color="Red (633nm)" package="5 mm [THT]"]
  LED15 = LED - 5mm [color="Red (633nm)" package="5 mm [THT]"]
  LED16 = LED - 5mm [color="Red (633nm)" package="5 mm [THT]"]
  LED17 = LED - 5mm [color="Red (633nm)" package="5 mm [THT]"]
  LED18 = LED - 5mm [color="Red (633nm)" package="5 mm [THT]"]
  LED19 = LED - 5mm [color="Red (633nm)" package="5 mm [THT]"]
  LED20 = LED - 5mm [color="Red (633nm)" package="5 mm [THT]"]
  LED21 = LED - 5mm [color="Red (633nm)" package="5 mm [THT]"]
  LED22 = LED - 5mm [color="Red (633nm)" package="5 mm [THT]"]
  LED23 = LED - 5mm [color="Red (633nm)" package="5 mm [THT]"]
  LED24 = LED - 5mm [color="Red (633nm)" package="5 mm [THT]"]
  LED25 = LED - 5mm [color="Red (633nm)" package="5 mm [THT]"]
  LED26 = LED - 5mm [color="Red (633nm)" package="5 mm [THT]"]
  LED27 = LED - 5mm [color="Red (633nm)" package="5 mm [THT]"]
  LED28 = LED - 5mm [color="Red (633nm)" package="5 mm [THT]"]
  LED29 = LED - 5mm [color="Red (633nm)" package="5 mm [THT]"]
  LED30 = LED - 5mm [color="Red (633nm)" package="5 mm [THT]"]
  LED31 = LED - 5mm [color="Red (633nm)" package="5 mm [THT]"]
  LED32 = LED - 5mm [color="Red (633nm)" package="5 mm [THT]"]
  LED33 = LED - 5mm [color="Red (633nm)" package="5 mm [THT]"]
  LED34 = LED - 5mm [color="Red (633nm)" package="5 mm [THT]"]
  LED35 = LED - 5mm [color="Red (633nm)" package="5 mm [THT]"]
  LED36 = LED - 5mm [color="Red (633nm)" package="5 mm [THT]"]
  LED37 = LED - 5mm [color="Red (633nm)" package="5 mm [THT]"]
  LED38 = LED - 5mm [color="Red (633nm)" package="5 mm [THT]"]
  LED39 = LED - 5mm [color="Red (633nm)" package="5 mm [THT]"]
  LED40 = LED - 5mm [color="Red (633nm)" package="5 mm [THT]"]
  LED41 = LED - 5mm [color="Red (633nm)" package="5 mm [THT]"]
  LED42 = LED - 5mm [color="Red (633nm)" package="5 mm [THT]"]
  LED43 = LED - 5mm [color="Red (633nm)" package="5 mm [THT]"]
  LED44 = LED - 5mm [color="Red (633nm)" package="5 mm [THT]"]
  LED45 = LED - 5mm [color="Red (633nm)" package="5 mm [THT]"]
  LED46 = LED - 5mm [color="Red (633nm)" package="5 mm [THT]"]
  LED47 = LED - 5mm [color="Red (633nm)" package="5 mm [THT]"]
  LED48 = LED - 5mm [color="Red (633nm)" package="5 mm [THT]"]
  LED49 = LED - 5mm [color="Red (633nm)" package="5 mm [THT]"]
  LED50 = LED - 5mm [color="Red (633nm)" package="5 mm [THT]"]
  LED51 = LED - 5mm [color="Red (633nm)" package="5 mm [THT]"]
  LED52 = LED - 5mm [color="Red (633nm)" package="5 mm [THT]"]
  LED53 = LED - 5mm [color="Red (633nm)" package="5 mm [THT]"]
  LED54 = LED - 5mm [color="Red (633nm)" package="5 mm [THT]"]
  LED55 = LED - 5mm [color="Red (633nm)" package="5 mm [THT]"]
  LED56 = LED - 5mm [color="Red (633nm)" package="5 mm [THT]"]
  LED57 = LED - 5mm [color="Red (633nm)" package="5 mm [THT]"]
  LED58 = LED - 5mm [color="Red (633nm)" package="5 mm [THT]"]
  LED59 = LED - 5mm [color="Red (633nm)" package="5 mm [THT]"]
  LED60 = LED - 5mm [color="Red (633nm)" package="5 mm [THT]"]
  LED61 = LED - 5mm [color="Red (633nm)" package="5 mm [THT]"]
  LED62 = LED - 5mm [color="Red (633nm)" package="5 mm [THT]"]
  LED63 = LED - 5mm [color="Red (633nm)" package="5 mm [THT]"]
  LED64 = LED - 5mm [color="Red (633nm)" package="5 mm [THT]"]
  LED65 = LED - 5mm [color="Red (633nm)" package="5 mm [THT]"]
  LED66 = LED - 5mm [color="Red (633nm)" package="5 mm [THT]"]
  LED67 = LED - 5mm [color="Red (633nm)" package="5 mm [THT]"]
  LED68 = LED - 5mm [color="Red (633nm)" package="5 mm [THT]"]
  LED69 = LED - 5mm [color="Red (633nm)" package="5 mm [THT]"]
  LED70 = LED - 5mm [color="Red (633nm)" package="5 mm [THT]"]
  LED71 = LED - 5mm [color="Red (633nm)" package="5 mm [THT]"]
  LED72 = LED - 5mm [color="Red (633nm)" package="5 mm [THT]"]
  LED73 = LED - 5mm [color="Red (633nm)" package="5 mm [THT]"]
  LED74 = LED - 5mm [color="Red (633nm)" package="5 mm [THT]"]
  LED75 = LED - 5mm [color="Red (633nm)" package="5 mm [THT]"]
  LED76 = LED - 5mm [color="Red (633nm)" package="5 mm [THT]"]
  LED77 = LED - 5mm [color="Red (633nm)" package="5 mm [THT]"]
  LED78 = LED - 5mm [color="Red (633nm)" package="5 mm [THT]"]
  LED79 = LED - 5mm [color="Red (633nm)" package="5 mm [THT]"]
  LED80 = LED - 5mm [color="Red (633nm)" package="5 mm [THT]"]
  LED81 = LED - 5mm [color="Red (633nm)" package="5 mm [THT]"]
  LED82 = LED - 5mm [color="Red (633nm)" package="5 mm [THT]"]
  LED83 = LED - 5mm [color="Red (633nm)" package="5 mm [THT]"]
  LED84 = LED - 5mm [color="Red (633nm)" package="5 mm [THT]"]
  LED85 = LED - 5mm [color="Red (633nm)" package="5 mm [THT]"]
  LED86 = LED - 5mm [color="Red (633nm)" package="5 mm [THT]"]
  LED87 = LED - 5mm [color="Red (633nm)" package="5 mm [THT]"]
  LED88 = LED - 5mm [color="Red (633nm)" package="5 mm [THT]"]
  LED89 = LED - 5mm [color="Red (633nm)" package="5 mm [THT]"]
  LED90 = LED - 5mm [color="Red (633nm)" package="5 mm [THT]"]
  LED91 = LED - 5mm [color="Red (633nm)" package="5 mm [THT]"]
  LED92 = LED - 5mm [color="Red (633nm)" package="5 mm [THT]"]
  LED93 = LED - 5mm [color="Red (633nm)" package="5 mm [THT]"]
  LED94 = LED - 5mm [color="Red (633nm)" package="5 mm [THT]"]
  LED95 = LED - 5mm [color="Red (633nm)" package="5 mm [THT]"]
  LED96 = LED - 5mm [color="Red (633nm)" package="5 mm [THT]"]
  LED97 = LED - 5mm [color="Red (633nm)" package="5 mm [THT]"]
  LED98 = LED - 5mm [color="Red (633nm)" package="5 mm [THT]"]
  LED99 = LED - 5mm [color="Red (633nm)" package="5 mm [THT]"]
  LED100 = LED - 5mm [color="Red (633nm)" package="5 mm [THT]"]
  LED101 = LED - 5mm [color="Red (633nm)" package="5 mm [THT]"]
  LED102 = LED - 5mm [color="Red (633nm)" package="5 mm [THT]"]
  LED103 = LED - 5mm [color="Red (633nm)" package="5 mm [THT]"]
  LED104 = LED - 5mm [color="Red (633nm)" package="5 mm [THT]"]
  LED105 = LED - 5mm [color="Red (633nm)" package="5 mm [THT]"]
  LED106 = LED - 5mm [color="Red (633nm)" package="5 mm [THT]"]
  LED107 = LED - 5mm [color="Red (633nm)" package="5 mm [THT]"]
  LED108 = LED - 5mm [color="Red (633nm)" package="5 mm [THT]"]
  LED109 = LED - 5mm [color="Red (633nm)" package="5 mm [THT]"]
  LED110 = LED - 5mm [color="Red (633nm)" package="5 mm [THT]"]
  LED111 = LED - 5mm [color="Red (633nm)" package="5 mm [THT]"]
  LED112 = LED - 5mm [color="Red (633nm)" package="5 mm [THT]"]
  LED113 = LED - 5mm [color="Red (633nm)" package="5 mm [THT]"]
  LED114 = LED - 5mm [color="Red (633nm)" package="5 mm [THT]"]
  LED115 = LED - 5mm [color="Red (633nm)" package="5 mm [THT]"]
  LED116 = LED - 5mm [color="Red (633nm)" package="5 mm [THT]"]
  LED117 = LED - 5mm [color="Red (633nm)" package="5 mm [THT]"]
  LED118 = LED - 5mm [color="Red (633nm)" package="5 mm [THT]"]
  LED119 = LED - 5mm [color="Red (633nm)" package="5 mm [THT]"]
  LED120 = LED - 5mm [color="Red (633nm)" package="5 mm [THT]"]
  LED121 = LED - 5mm [color="Red (633nm)" package="5 mm [THT]"]
  LED122 = LED - 5mm [color="Red (633nm)" package="5 mm [THT]"]
  LED123 = LED - 5mm [color="Red (633nm)" package="5 mm [THT]"]
  LED124 = LED - 5mm [color="Red (633nm)" package="5 mm [THT]"]
  LED125 = LED - 5mm [color="Red (633nm)" package="5 mm [THT]"]
  LED126 = LED - 5mm [color="Red (633nm)" package="5 mm [THT]"]
  LED127 = LED - 5mm [color="Red (633nm)" package="5 mm [THT]"]
  LED128 = LED - 5mm [color="Red (633nm)" package="5 mm [THT]"]
  LED129 = LED - 5mm [color="Red (633nm)" package="5 mm [THT]"]
  LED130 = LED - 5mm [color="Red (633nm)" package="5 mm [THT]"]
  LED131 = LED - 5mm [color="Red (633nm)" package="5 mm [THT]"]
  LED132 = LED - 5mm [color="Red (633nm)" package="5 mm [THT]"]
  LED133 = LED - 5mm [color="Red (633nm)" package="5 mm [THT]"]
  LED134 = LED - 5mm [color="Red (633nm)" package="5 mm [THT]"]
  LED135 = LED - 5mm [color="Red (633nm)" package="5 mm [THT]"]
  LED136 = LED - 5mm [color="Red (633nm)" package="5 mm [THT]"]
  LED137 = LED - 5mm [color="Red (633nm)" package="5 mm [THT]"]
  LED138 = LED - 5mm [color="Red (633nm)" package="5 mm [THT]"]
  LED139 = LED - 5mm [color="Red (633nm)" package="5 mm [THT]"]
  LED140 = LED - 5mm [color="Red (633nm)" package="5 mm [THT]"]
  LED141 = LED - 5mm [color="Red (633nm)" package="5 mm [THT]"]
  LED142 = LED - 5mm [color="Red (633nm)" package="5 mm [THT]"]
  LED143 = LED - 5mm [color="Red (633nm)" package="5 mm [THT]"]
  LED144 = LED - 5mm [color="Red (633nm)" package="5 mm [THT]"]
  LED145 = LED - 5mm [color="Red (633nm)" package="5 mm [THT]"]
  LED146 = LED - 5mm [color="Red (633nm)" package="5 mm [THT]"]
  LED147 = LED - 5mm [color="Red (633nm)" package="5 mm [THT]"]
  LED148 = LED - 5mm [color="Red (633nm)" package="5 mm [THT]"]
  LED149 = LED - 5mm [color="Red (633nm)" package="5 mm [THT]"]
  LED150 = LED - 5mm [color="Red (633nm)" package="5 mm [THT]"]
  LED151 = LED - 5mm [color="Red (633nm)" package="5 mm [THT]"]
  LED152 = LED - 5mm [color="Red (633nm)" package="5 mm [THT]"]
  LED153 = LED - 5mm [color="Red (633nm)" package="5 mm [THT]"]
  LED154 = LED - 5mm [color="Red (633nm)" package="5 mm [THT]"]
  LED155 = LED - 5mm [color="Red (633nm)" package="5 mm [THT]"]
  LED156 = LED - 5mm [color="Red (633nm)" package="5 mm [THT]"]
  LED157 = LED - 5mm [color="Red (633nm)" package="5 mm [THT]"]
  LED158 = LED - 5mm [color="Red (633nm)" package="5 mm [THT]"]
  LED159 = LED - 5mm [color="Red (633nm)" package="5 mm [THT]"]
  LED160 = LED - 5mm [color="Red (633nm)" package="5 mm [THT]"]
  LED161 = LED - 5mm [color="Red (633nm)" package="5 mm [THT]"]
  LED162 = LED - 5mm [color="Red (633nm)" package="5 mm [THT]"]
  LED163 = LED - 5mm [color="Red (633nm)" package="5 mm [THT]"]
  LED164 = LED - 5mm [color="Red (633nm)" package="5 mm [THT]"]
  LED165 = LED - 5mm [color="Red (633nm)" package="5 mm [THT]"]
  LED166 = LED - 5mm [color="Red (633nm)" package="5 mm [THT]"]
  LED167 = LED - 5mm [color="Red (633nm)" package="5 mm [THT]"]
  LED168 = LED - 5mm [color="Red (633nm)" package="5 mm [THT]"]
  LED169 = LED - 5mm [color="Red (633nm)" package="5 mm [THT]"]
  LED170 = LED - 5mm [color="Red (633nm)" package="5 mm [THT]"]
  LED171 = LED - 5mm [color="Red (633nm)" package="5 mm [THT]"]
  LED172 = LED - 5mm [color="Red (633nm)" package="5 mm [THT]"]
  LED173 = LED - 5mm [color="Red (633nm)" package="5 mm [THT]"]
  LED174 = LED - 5mm [color="Red (633nm)" package="5 mm [THT]"]
  LED175 = LED - 5mm [color="Red (633nm)" package="5 mm [THT]"]
  LED176 = LED - 5mm [color="Red (633nm)" package="5 mm [THT]"]
  LED177 = LED - 5mm [color="Red (633nm)" package="5 mm [THT]"]
  LED178 = LED - 5mm [color="Red (633nm)" package="5 mm [THT]"]
  LED179 = LED - 5mm [color="Red (633nm)" package="5 mm [THT]"]
  LED180 = LED - 5mm [color="Red (633nm)" package="5 mm [THT]"]
  LED181 = LED - 5mm [color="Red (633nm)" package="5 mm [THT]"]
  LED182 = LED - 5mm [color="Red (633nm)" package="5 mm [THT]"]
  LED183 = LED - 5mm [color="Red (633nm)" package="5 mm [THT]"]
  LED184 = LED - 5mm [color="Red (633nm)" package="5 mm [THT]"]
  LED185 = LED - 5mm [color="Red (633nm)" package="5 mm [THT]"]
  LED186 = LED - 5mm [color="Red (633nm)" package="5 mm [THT]"]
  LED187 = LED - 5mm [color="Red (633nm)" package="5 mm [THT]"]
  LED188 = LED - 5mm [color="Red (633nm)" package="5 mm [THT]"]
  LED189 = LED - 5mm [color="Red (633nm)" package="5 mm [THT]"]
  LED190 = LED - 5mm [color="Red (633nm)" package="5 mm [THT]"]
  LED191 = LED - 5mm [color="Red (633nm)" package="5 mm [THT]"]
  LED192 = LED - 5mm [color="Red (633nm)" package="5 mm [THT]"]
  LED193 = LED - 5mm [color="Red (633nm)" package="5 mm [THT]"]
  LED194 = LED - 5mm [color="Red (633nm)" package="5 mm [THT]"]
  LED195 = LED - 5mm [color="Red (633nm)" package="5 mm [THT]"]
  LED196 = LED - 5mm [color="Red (633nm)" package="5 mm [THT]"]
  LED197 = LED - 5mm [color="Red (633nm)" package="5 mm [THT]"]
  LED198 = LED - 5mm [color="Red (633nm)" package="5 mm [THT]"]
  LED199 = LED - 5mm [color="Red (633nm)" package="5 mm [THT]"]
  LED200 = LED - 5mm [color="Red (633nm)" package="5 mm [THT]"]
  LED201 = LED - 5mm [color="Red (633nm)" package="5 mm [THT]"]
  LED202 = LED - 5mm [color="Red (633nm)" package="5 mm [THT]"]
  LED203 = LED - 5mm [color="Red (633nm)" package="5 mm [THT]"]
  LED204 = LED - 5mm [color="Red (633nm)" package="5 mm [THT]"]
  LED205 = LED - 5mm [color="Red (633nm)" package="5 mm [THT]"]
  LED206 = LED - 5mm [color="Red (633nm)" package="5 mm [THT]"]
  LED207 = LED - 5mm [color="Red (633nm)" package="5 mm [THT]"]
  LED208 = LED - 5mm [color="Red (633nm)" package="5 mm [THT]"]
  LED209 = LED - 5mm [color="Red (633nm)" package="5 mm [THT]"]
  LED210 = LED - 5mm [color="Red (633nm)" package="5 mm [THT]"]
  LED211 = LED - 5mm [color="Red (633nm)" package="5 mm [THT]"]
  LED212 = LED - 5mm [color="Red (633nm)" package="5 mm [THT]"]
  LED213 = LED - 5mm [color="Red (633nm)" package="5 mm [THT]"]
  LED214 = LED - 5mm [color="Red (633nm)" package="5 mm [THT]"]
  LED215 = LED - 5mm [color="Red (633nm)" package="5 mm [THT]"]
  LED216 = LED - 5mm [color="Red (633nm)" package="5 mm [THT]"]
  LED217 = LED - 5mm [color="Red (633nm)" package="5 mm [THT]"]
  LED218 = LED - 5mm [color="Red (633nm)" package="5 mm [THT]"]
  LED219 = LED - 5mm [color="Red (633nm)" package="5 mm [THT]"]
  LED220 = LED - 5mm [color="Red (633nm)" package="5 mm [THT]"]
  LED221 = LED - 5mm [color="Red (633nm)" package="5 mm [THT]"]
  LED222 = LED - 5mm [color="Red (633nm)" package="5 mm [THT]"]
  LED223 = LED - 5mm [color="Red (633nm)" package="5 mm [THT]"]
  LED224 = LED - 5mm [color="Red (633nm)" package="5 mm [THT]"]
  LED225 = LED - 5mm [color="Red (633nm)" package="5 mm [THT]"]
  LED226 = LED - 5mm [color="Red (633nm)" package="5 mm [THT]"]
  LED227 = LED - 5mm [color="Red (633nm)" package="5 mm [THT]"]
  LED228 = LED - 5mm [color="Red (633nm)" package="5 mm [THT]"]
  LED229 = LED - 5mm [color="Red (633nm)" package="5 mm [THT]"]
  LED230 = LED - 5mm [color="Red (633nm)" package="5 mm [THT]"]
  LED231 = LED - 5mm [color="Red (633nm)" package="5 mm [THT]"]
  LED232 = LED - 5mm [color="Red (633nm)" package="5 mm [THT]"]
  LED233 = LED - 5mm [color="Red (633nm)" package="5 mm [THT]"]
  LED234 = LED - 5mm [color="Red (633nm)" package="5 mm [THT]"]
  LED235 = LED - 5mm [color="Red (633nm)" package="5 mm [THT]"]
  LED236 = LED - 5mm [color="Red (633nm)" package="5 mm [THT]"]
  LED237 = LED - 5mm [color="Red (633nm)" package="5 mm [THT]"]
  LED238 = LED - 5mm [color="Red (633nm)" package="5 mm [THT]"]
  LED239 = LED - 5mm [color="Red (633nm)" package="5 mm [THT]"]
  LED240 = LED - 5mm [color="Red (633nm)" package="5 mm [THT]"]
  IC1 = IC, DIP package, 14 pins [chip_label=74LS164]
  IC2 = IC, DIP package, 14 pins [chip_label=74LS164]
  IC3 = IC, DIP package, 14 pins [chip_label=74LS164]
  IC4 = IC, DIP package, 14 pins [chip_label=74LS164]
  IC5 = IC, DIP package, 18 pins [chip_label=ULN2003A]
  IC6 = IC, DIP package, 18 pins [chip_label=ULN2003A]
  IC7 = IC, DIP package, 18 pins [chip_label=ULN2003A]
  IC8 = IC, DIP package, 18 pins [chip_label=ULN2003A]
  R1 = Resistor [tolerance=±5% resistance=10 package=THT]
  R2 = Resistor [tolerance=±5% resistance=10 package=THT]
  R3 = Resistor [tolerance=±5% resistance=10 package=THT]
  R4 = Resistor [tolerance=±5% resistance=10 package=THT]
  R5 = Resistor [tolerance=±5% resistance=10 package=THT]
  R6 = Resistor [tolerance=±5% resistance=10 package=THT]
  R7 = Resistor [tolerance=±5% resistance=10 package=THT]
  R8 = Resistor [tolerance=±5% resistance=10 package=THT]
  R9 = Resistor [tolerance=±5% resistance=10 package=THT]
  R10 = Resistor [tolerance=±5% resistance=10 package=THT]
  R11 = Resistor [tolerance=±5% resistance=10 package=THT]
  R12 = Resistor [tolerance=±5% resistance=10 package=THT]
  R13 = Resistor [tolerance=±5% resistance=10 package=THT]
  R14 = Resistor [tolerance=±5% resistance=10 package=THT]
  R15 = Resistor [tolerance=±5% resistance=10 package=THT]
  R16 = Resistor [tolerance=±5% resistance=10 package=THT]
  R17 = Resistor [tolerance=±5% resistance=10 package=THT]
  R18 = Resistor [tolerance=±5% resistance=10 package=THT]
  R19 = Resistor [tolerance=±5% resistance=10 package=THT]
  R20 = Resistor [tolerance=±5% resistance=10 package=THT]
  R21 = Resistor [tolerance=±5% resistance=10 package=THT]
  R22 = Resistor [tolerance=±5% resistance=10 package=THT]
  R23 = Resistor [tolerance=±5% resistance=10 package=THT]
  R24 = Resistor [tolerance=±5% resistance=10 package=THT]
  R25 = Resistor [tolerance=±5% resistance=10 package=THT]
  R26 = Resistor [tolerance=±5% resistance=10 package=THT]
  R27 = Resistor [tolerance=±5% resistance=10 package=THT]
  R29 = Resistor [tolerance=±5% resistance=10 package=THT]
  R31 = Resistor [tolerance=±5% resistance=10 package=THT]
  R32 = Resistor [tolerance=±5% resistance=10 package=THT]
  R33 = Resistor [tolerance=±5% resistance=120 package=THT]
  R34 = Resistor [tolerance=±5% resistance=120 package=THT]
  R35 = Resistor [tolerance=±5% resistance=120 package=THT]
  R36 = Resistor [tolerance=±5% resistance=120 package=THT]
  R37 = Resistor [tolerance=±5% resistance=120 package=THT]
  R38 = Resistor [tolerance=±5% resistance=120 package=THT]
  R39 = Resistor [tolerance=±5% resistance=120 package=THT]
  R40 = Resistor [tolerance=±5% resistance=120 package=THT]
  Q2 = PNP-Transistor [part_number=BD678 package="TO92 [THT]"]
  Q3 = PNP-Transistor [part_number=BD678 package="TO92 [THT]"]
  Q4 = PNP-Transistor [part_number=BD678 package="TO92 [THT]"]
  Q5 = PNP-Transistor [part_number=BD678 package="TO92 [THT]"]
  Q6 = PNP-Transistor [part_number=BD678 package="TO92 [THT]"]
  Q7 = PNP-Transistor [part_number=BD678 package="TO92 [THT]"]
  Q8 = PNP-Transistor [part_number=BD678 package="TO92 [THT]"]
  Q1 = PNP-Transistor [part_number=BD678 package="TO92 [THT]"]

nets:
  N1: LED1.cathode, LED9.cathode, LED22.cathode, LED39.cathode, LED42.cathode, LED47.cathode, LED58.cathode, LED59.cathode, LED62.cathode, LED69.cathode, LED76.cathode, LED90.cathode, LED103.cathode, LED106.cathode, LED126.cathode, LED130.cathode, LED131.cathode, LED139.cathode, LED141.cathode, LED147.cathode, LED149.cathode, LED169.cathode, LED178.cathode, LED192.cathode, LED201.cathode, LED204.cathode, LED209.cathode, LED210.cathode, LED218.cathode, LED237.cathode, Q8.E
  N2: LED1.anode, LED2.anode, LED3.anode, LED4.anode, LED5.anode, LED6.anode, LED7.anode, LED8.anode, R1.Pin_1
  N3: LED2.cathode, LED16.cathode, LED20.cathode, LED26.cathode, LED27.cathode, LED37.cathode, LED52.cathode, LED53.cathode, LED79.cathode, LED80.cathode, LED81.cathode, LED83.cathode, LED97.cathode, LED110.cathode, LED119.cathode, LED122.cathode, LED133.cathode, LED135.cathode, LED142.cathode, LED145.cathode, LED152.cathode, LED156.cathode, LED157.cathode, LED187.cathode, LED199.cathode, LED203.cathode, LED208.cathode, LED219.cathode, LED222.cathode, LED234.cathode, Q7.E
  N4: LED3.cathode, LED15.cathode, LED18.cathode, LED29.cathode, LED38.cathode, LED40.cathode, LED68.cathode, LED73.cathode, LED75.cathode, LED78.cathode, LED88.cathode, LED93.cathode, LED101.cathode, LED111.cathode, LED118.cathode, LED136.cathode, LED140.cathode, LED166.cathode, LED170.cathode, LED174.cathode, LED175.cathode, LED176.cathode, LED177.cathode, LED185.cathode, LED195.cathode, LED196.cathode, LED205.cathode, LED216.cathode, LED217.cathode, LED235.cathode, Q6.E
  N5: LED4.cathode, LED11.cathode, LED21.cathode, LED44.cathode, LED45.cathode, LED46.cathode, LED51.cathode, LED63.cathode, LED70.cathode, LED86.cathode, LED91.cathode, LED96.cathode, LED102.cathode, LED107.cathode, LED113.cathode, LED120.cathode, LED134.cathode, LED153.cathode, LED160.cathode, LED163.cathode, LED164.cathode, LED167.cathode, LED168.cathode, LED183.cathode, LED197.cathode, LED200.cathode, LED207.cathode, LED211.cathode, LED221.cathode, LED240.cathode, Q5.E
  N6: LED5.cathode, LED10.cathode, LED19.cathode, LED25.cathode, LED34.cathode, LED36.cathode, LED55.cathode, LED64.cathode, LED67.cathode, LED72.cathode, LED89.cathode, LED92.cathode, LED99.cathode, LED100.cathode, LED108.cathode, LED112.cathode, LED116.cathode, LED158.cathode, LED162.cathode, LED172.cathode, LED180.cathode, LED181.cathode, LED182.cathode, LED191.cathode, LED202.cathode, LED224.cathode, LED225.cathode, LED230.cathode, LED233.cathode, LED236.cathode, Q4.E
  N7: LED6.cathode, LED14.cathode, LED17.cathode, LED30.cathode, LED32.cathode, LED33.cathode, LED49.cathode, LED56.cathode, LED77.cathode, LED82.cathode, LED84.cathode, LED85.cathode, LED98.cathode, LED105.cathode, LED109.cathode, LED121.cathode, LED125.cathode, LED143.cathode, LED144.cathode, LED148.cathode, LED150.cathode, LED151.cathode, LED159.cathode, LED186.cathode, LED193.cathode, LED214.cathode, LED223.cathode, LED228.cathode, LED229.cathode, LED231.cathode, Q3.E
  N8: LED7.cathode, LED12.cathode, LED24.cathode, LED31.cathode, LED35.cathode, LED41.cathode, LED57.cathode, LED60.cathode, LED61.cathode, LED74.cathode, LED87.cathode, LED95.cathode, LED104.cathode, LED115.cathode, LED117.cathode, LED123.cathode, LED124.cathode, LED127.cathode, LED128.cathode, LED132.cathode, LED154.cathode, LED161.cathode, LED184.cathode, LED188.cathode, LED198.cathode, LED206.cathode, LED220.cathode, LED227.cathode, LED232.cathode, LED239.cathode, Q2.E
  N9: LED8.cathode, LED13.cathode, LED23.cathode, LED28.cathode, LED43.cathode, LED48.cathode, LED50.cathode, LED54.cathode, LED65.cathode, LED66.cathode, LED71.cathode, LED94.cathode, LED114.cathode, LED129.cathode, LED137.cathode, LED138.cathode, LED146.cathode, LED155.cathode, LED165.cathode, LED171.cathode, LED173.cathode, LED179.cathode, LED189.cathode, LED190.cathode, LED194.cathode, LED212.cathode, LED213.cathode, LED215.cathode, LED226.cathode, LED238.cathode, Q1.E
  N10: LED9.anode, LED10.anode, LED11.anode, LED12.anode, LED13.anode, LED14.anode, LED15.anode, LED16.anode, R2.Pin_1
  N11: LED17.anode, LED18.anode, LED19.anode, LED20.anode, LED21.anode, LED22.anode, LED23.anode, LED24.anode, R3.Pin_1
  N12: LED25.anode, LED31.anode, LED33.anode, LED37.anode, LED38.anode, LED46.anode, LED47.anode, LED48.anode, R6.Pin_1
  N13: LED26.anode, LED28.anode, LED32.anode, LED34.anode, LED40.anode, LED41.anode, LED42.anode, LED44.anode, R5.Pin_1
  N14: LED27.anode, LED29.anode, LED30.anode, LED35.anode, LED36.anode, LED39.anode, LED43.anode, LED45.anode, R4.Pin_1
  N15: LED49.anode, LED52.anode, LED55.anode, LED63.anode, LED69.anode, LED74.anode, LED88.anode, LED94.anode, R7.Pin_1
  N16: LED50.anode, LED58.anode, LED68.anode, LED77.anode, LED83.anode, LED87.anode, LED91.anode, LED92.anode, R14.Pin_1
  N17: LED51.anode, LED54.anode, LED56.anode, LED59.anode, LED72.anode, LED81.anode, LED93.anode, LED95.anode, R8.Pin_1
  N18: LED53.anode, LED61.anode, LED62.anode, LED64.anode, LED65.anode, LED73.anode, LED82.anode, LED96.anode, R13.Pin_1
  N19: LED57.anode, LED67.anode, LED71.anode, LED75.anode, LED80.anode, LED84.anode, LED86.anode, LED90.anode, R11.Pin_1
  N20: LED60.anode, LED66.anode, LED70.anode, LED76.anode, LED78.anode, LED79.anode, LED85.anode, LED89.anode, R10.Pin_1
  N21: LED97.anode, LED100.anode, LED101.anode, LED114.anode, LED132.anode, LED151.anode, LED167.anode, LED169.anode, R15.Pin_1
  N22: LED98.anode, LED124.anode, LED138.anode, LED145.anode, LED147.anode, LED162.anode, LED175.anode, LED183.anode, R18.Pin_1
  N23: LED99.anode, LED102.anode, LED117.anode, LED122.anode, LED141.anode, LED159.anode, LED174.anode, LED190.anode, R22.Pin_1
  N24: LED103.anode, LED125.anode, LED157.anode, LED160.anode, LED172.anode, LED176.anode, LED188.anode, LED189.anode, R17.Pin_1
  N25: LED104.anode, LED107.anode, LED131.anode, LED148.anode, LED155.anode, LED156.anode, LED158.anode, LED170.anode, R20.Pin_1
  N26: LED105.anode, LED113.anode, LED135.anode, LED136.anode, LED161.anode, LED165.anode, LED178.anode, LED191.anode, R23.Pin_1
  N27: LED106.anode, LED112.anode, LED115.anode, LED140.anode, LED150.anode, LED168.anode, LED179.anode, LED187.anode, R12.Pin_1
  N28: LED108.anode, LED127.anode, LED133.anode, LED149.anode, LED163.anode, LED171.anode, LED177.anode, LED186.anode, R24.Pin_1
  N29: LED109.anode, LED110.anode, LED111.anode, LED123.anode, LED130.anode, LED146.anode, LED164.anode, LED180.anode, R16.Pin_1
  N30: LED116.anode, LED120.anode, LED139.anode, LED142.anode, LED143.anode, LED154.anode, LED166.anode, LED173.anode, R19.Pin_1
  N31: LED118.anode, LED121.anode, LED134.anode, LED137.anode, LED152.anode, LED182.anode, LED184.anode, LED192.anode, R9.Pin_1
  N32: LED119.anode, LED126.anode, LED128.anode, LED129.anode, LED144.anode, LED153.anode, LED181.anode, LED185.anode, R21.Pin_1
  N33: LED193.anode, LED195.anode, LED203.anode, LED209.anode, LED212.anode, LED220.anode, LED221.anode, LED233.anode, R29.Pin_1
  N34: LED194.anode, LED201.anode, LED205.anode, LED208.anode, LED211.anode, LED229.anode, LED230.anode, LED232.anode, R26.Pin_1
  N35: LED196.anode, LED207.anode, LED218.anode, LED219.anode, LED224.anode, LED228.anode, LED238.anode, LED239.anode, R25.Pin_1
  N36: LED197.anode, LED198.anode, LED199.anode, LED210.anode, LED214.anode, LED226.anode, LED235.anode, LED236.anode, R31.Pin_1
  N37: LED200.anode, LED202.anode, LED215.anode, LED216.anode, LED222.anode, LED223.anode, LED227.anode, LED237.anode, R27.Pin_1
  N38: LED204.anode, LED206.anode, LED213.anode, LED217.anode, LED225.anode, LED231.anode, LED234.anode, LED240.anode, R32.Pin_1
  A+B: IC1.pin1, IC1.pin2, IC4.pin11, IC8.pin5
  N39: IC1.pin3, IC5.pin4
  N40: IC1.pin4, IC5.pin3
  N41: IC1.pin5, IC5.pin2
  N42: IC1.pin6, IC5.pin1
  GND: IC1.pin7, IC2.pin7, IC3.pin7, IC4.pin7, IC5.pin9, IC6.pin9, IC7.pin9, IC8.pin9
  CLOCK: IC1.pin8, IC2.pin8, IC3.pin8, IC4.pin8
  NOT CLEAR: IC1.pin9, IC2.pin9, IC3.pin9, IC4.pin9
  N43: IC1.pin10, IC5.pin8
  N44: IC1.pin11, IC5.pin7
  N45: IC1.pin12, IC5.pin6
  N46: IC1.pin13, IC2.pin1, IC2.pin2, IC5.pin5
  Vcc (+5v): IC1.pin14, IC2.pin14, IC3.pin14, IC4.pin14
  N47: IC2.pin3, IC6.pin4
  N48: IC2.pin4, IC6.pin3
  N49: IC2.pin5, IC6.pin2
  N50: IC2.pin6, IC6.pin1
  N51: IC2.pin10, IC6.pin8
  N52: IC2.pin11, IC6.pin7
  N53: IC2.pin12, IC6.pin6
  N54: IC2.pin13, IC3.pin1, IC3.pin2, IC6.pin5
  N55: IC3.pin3, IC7.pin4
  N56: IC3.pin4, IC7.pin3
  N57: IC3.pin5, IC7.pin2
  N58: IC3.pin6, IC7.pin1
  N59: IC3.pin10, IC7.pin8
  N60: IC3.pin11, IC7.pin7
  N61: IC3.pin12, IC7.pin6
  N62: IC3.pin13, IC4.pin1, IC4.pin2, IC7.pin5
  N63: IC4.pin3, IC8.pin2
  N64: IC4.pin4, IC8.pin1
  N65: IC4.pin5, IC8.pin8
  N66: IC4.pin6, IC8.pin7
  N67: IC4.pin10, IC8.pin6
  COM: IC5.pin10, IC6.pin10, IC7.pin10, IC8.pin10
  N68: IC5.pin11, R5.Pin_0
  N69: IC5.pin12, R6.Pin_0
  N70: IC5.pin13, R7.Pin_0
  N71: IC5.pin14, R8.Pin_0
  N72: IC5.pin15, R1.Pin_0
  N73: IC5.pin16, R2.Pin_0
  N74: IC5.pin17, R3.Pin_0
  N75: IC5.pin18, R4.Pin_0
  N76: IC6.pin11, R9.Pin_0
  N77: IC6.pin12, R15.Pin_0
  N78: IC6.pin13, R12.Pin_0
  N79: IC6.pin14, R16.Pin_0
  N80: IC6.pin15, R10.Pin_0
  N81: IC6.pin16, R13.Pin_0
  N82: IC6.pin17, R11.Pin_0
  N83: IC6.pin18, R14.Pin_0
  N84: IC7.pin11, R23.Pin_0
  N85: IC7.pin12, R24.Pin_0
  N86: IC7.pin13, R21.Pin_0
  N87: IC7.pin14, R17.Pin_0
  N88: IC7.pin15, R22.Pin_0
  N89: IC7.pin16, R20.Pin_0
  N90: IC7.pin17, R18.Pin_0
  N91: IC7.pin18, R19.Pin_0
  N92: IC8.pin11, R27.Pin_0
  N93: IC8.pin12, R26.Pin_0
  N94: IC8.pin13, R31.Pin_0
  N95: IC8.pin14, R25.Pin_0
  N96: IC8.pin17, R29.Pin_0
  N97: IC8.pin18, R32.Pin_0
  ROW1: R33.Pin_0
  N98: R33.Pin_1, Q1.B
  ROW2: R34.Pin_0
  N99: R34.Pin_1, Q2.B
  ROW3: R35.Pin_0
  N100: R35.Pin_1, Q3.B
  ROW4: R36.Pin_0
  N101: R36.Pin_1, Q4.B
  ROW5: R37.Pin_0
  N102: R37.Pin_1, Q5.B
  ROW6: R38.Pin_0
  N103: R38.Pin_1, Q6.B
  ROW7: R39.Pin_0
  N104: R39.Pin_1, Q7.B
  ROW8: R40.Pin_0
  N105: R40.Pin_1, Q8.B
  Vs BUS: Q2.C, Q3.C, Q4.C, Q5.C, Q6.C, Q7.C, Q8.C, Q1.C

notes:
  Moving LED Sign, DSSC  /  Drawing by Richard Morris, 1.0.0.0A
  PL4 pin-outs
  top row:
  CLOCK
  NOT CLEAR
  GND/1
  GND/2
  GND/3
  bottom row:
  Vcc (+5 volts)
  A+B (data)
  GND/4
  GND/5
  GND/6
  PL3 pin-outs
  top row:
  ROW 7
  ROW 5
  ROW 3
  ROW 1
  Vs/1 (7.5 volts)
  Vs/2
  Vs/3
  bottom row:
  ROW 8
  ROW 6
  ROW 4
  ROW 2
  Vs/4 (7.5 volts)
  Vs/5
  Vs/6
  N/C
